// Logisim project 20250228.circ as structural Verilog: 3 circuits, main circuit main
module main (
  input  [3:0] A,
  input  [1:0] B,
  input  [3:0] in_3,
  input  [3:0] in_4
);

  DIR dir_1 (.A(A), .B(B), .out_3(in_3));
  ESQ esq_1 (.A(A), .B(B), .out_3(in_4));
endmodule

module DIR (
  input  [3:0] A,
  input  [1:0] B,
  output [3:0] out_3
);

  wire and_1_out, and_2_out, and_3_out, and_4_out, and_5_out, and_6_out, and_7_out, and_8_out, and_9_out;

  and and_1 (and_1_out, A[3], B[1], B[0]);
  and and_2 (and_2_out, A[2], B[1], ~B[0]);  // AND_Gate
  and and_3 (and_3_out, A[1], ~B[1], B[0]);  // AND_Gate
  and and_4 (and_4_out, A[0], ~B[1], ~B[0]);  // AND_Gate
  and and_5 (and_5_out, A[3], B[1], ~B[0]);  // AND_Gate
  and and_6 (and_6_out, A[2], ~B[1], B[0]);  // AND_Gate
  and and_7 (and_7_out, A[1], ~B[1], ~B[0]);  // AND_Gate
  and and_8 (and_8_out, A[3], ~B[1], B[0]);  // AND_Gate
  and and_9 (and_9_out, A[2], ~B[1], ~B[0]);  // AND_Gate
  and and_10 (out_3[3], A[3], ~B[1], ~B[0]);  // AND_Gate
  or or_1 (out_3[0], and_1_out, and_2_out, and_3_out, and_4_out);
  or or_2 (out_3[1], and_5_out, and_6_out, and_7_out);
  or or_3 (out_3[2], and_8_out, and_9_out);
endmodule

module ESQ (
  input  [3:0] A,
  input  [1:0] B,
  output [3:0] out_3
);

  wire and_1_out, and_2_out, and_3_out, and_4_out, and_5_out, and_6_out, and_7_out, and_8_out, and_9_out;

  and and_1 (and_1_out, A[0], B[1], B[0]);
  and and_2 (and_2_out, A[1], B[1], ~B[0]);  // AND_Gate
  and and_3 (and_3_out, A[2], ~B[1], B[0]);  // AND_Gate
  and and_4 (and_4_out, A[3], ~B[1], ~B[0]);  // AND_Gate
  and and_5 (and_5_out, A[0], B[1], ~B[0]);  // AND_Gate
  and and_6 (and_6_out, A[1], ~B[1], B[0]);  // AND_Gate
  and and_7 (and_7_out, A[2], ~B[1], ~B[0]);  // AND_Gate
  and and_8 (and_8_out, A[0], ~B[1], B[0]);  // AND_Gate
  and and_9 (and_9_out, A[1], ~B[1], ~B[0]);  // AND_Gate
  and and_10 (out_3[0], A[0], ~B[1], ~B[0]);  // AND_Gate
  or or_1 (out_3[3], and_1_out, and_2_out, and_3_out, and_4_out);
  or or_2 (out_3[2], and_5_out, and_6_out, and_7_out);
  or or_3 (out_3[1], and_8_out, and_9_out);
endmodule
