// Logisim project projeto-cpu-finalizado.circ as structural Verilog: 16 circuits, main circuit main
module main (
);

  wire clock_1_out, not_1_out, not_2_out, Overflow_q, Reset_out, ula_1_overflow, ula_1_zero,
       unidade_de_controle_1_clock_ac, unidade_de_controle_1_clock_ir, unidade_de_controle_1_clock_mem,
       unidade_de_controle_1_clock_pc, unidade_de_controle_1_d, unidade_de_controle_1_e,
       unidade_de_controle_1_load, unidade_de_controle_1_load_2, unidade_de_controle_1_reset_pc, Zero_q;
  wire [2:0] unidade_de_controle_1_opcode;
  wire [3:0] ac_1_q, mux_1_s, PC_q, ram_1_data, \ula_1_saída , unidade_de_controle_1_dados,
       unidade_de_controle_1_operando;
  wire [7:0] ir_1_q, rom_1_data;

  Counter #(.width(4), .max('hf), .trigger("falling")) PC (
    .load(unidade_de_controle_1_load_2), .D(unidade_de_controle_1_dados), .count(not_1_out), .Q(PC_q),
    .clk(unidade_de_controle_1_clock_pc), .clr(unidade_de_controle_1_reset_pc));  // open: carry
  not not_1 (not_1_out, unidade_de_controle_1_load_2);
  Clock clock_1 (.out(clock_1_out));
  Button Reset (.out(Reset_out));
  Unidade_de_Controle unidade_de_controle_1 (
    .Dados(unidade_de_controle_1_dados), .Operando(unidade_de_controle_1_operando),
    .D(unidade_de_controle_1_d), .OpCode(unidade_de_controle_1_opcode), .\INSTRUÇÃO (ir_1_q),
    .Clock_IR(unidade_de_controle_1_clock_ir), .Clock_PC(unidade_de_controle_1_clock_pc),
    .Clock_AC(unidade_de_controle_1_clock_ac), .Clock_MEM(unidade_de_controle_1_clock_mem),
    .Clock(clock_1_out), .Reset(Reset_out), .Reset_PC(unidade_de_controle_1_reset_pc), .ZERO(Zero_q),
    .Overflow(Overflow_q), .LOAD_2(unidade_de_controle_1_load_2), .load(unidade_de_controle_1_load),
    .E(unidade_de_controle_1_e));
  ROM #(.addrWidth(4)) rom_1 (.addr(PC_q), .data(rom_1_data));  // open: sel
  // Probe on ac_1_q
  // Probe on \ula_1_saída 
  // Probe on rom_1_data
  IR ir_1 (.D(rom_1_data), .Clock(unidade_de_controle_1_clock_ir), .Q(ir_1_q));
  // Probe on ir_1_q
  Mux mux_1 (.E0(unidade_de_controle_1_operando), .Controle(unidade_de_controle_1_d), .E1(ram_1_data), .S(mux_1_s));
  ULA ula_1 (
    .D(unidade_de_controle_1_e), .A(ac_1_q), .B(mux_1_s), .Overflow(ula_1_overflow),
    .\Operação (unidade_de_controle_1_opcode), .Zero(ula_1_zero), .\Saída (\ula_1_saída ));
  AC ac_1 (.D(\ula_1_saída ), .in_2(unidade_de_controle_1_clock_ac), .Q(ac_1_q));
  // Probe on mux_1_s
  not not_2 (not_2_out, unidade_de_controle_1_load);
  D_Flip_Flop Overflow (
    .clk(unidade_de_controle_1_clock_ac), .D(ula_1_overflow), .Q(Overflow_q));  // open: Qn, preset, en, reset
  D_Flip_Flop Zero (.clk(unidade_de_controle_1_clock_ac), .D(ula_1_zero), .Q(Zero_q));  // open: Qn, preset, en, reset
  RAM #(.addrWidth(4), .dataWidth(4)) ram_1 (
    .addr(unidade_de_controle_1_operando), .data(ram_1_data), .clk(unidade_de_controle_1_clock_mem),
    .ld(unidade_de_controle_1_load));  // open: sel, clr
  Buffer buffer_1 (.A(ac_1_q), .Control(not_2_out), .S(ram_1_data));

  // Notes on the sheet:
  //   MOV
  //   0
  //   000
  //   1
  //   000
  //   MOV
  //   2
  //   ADD
  //   001
  //   3
  //   001
  //   ADD
  //   010
  //   SUB
  //   4
  //   010
  //   SUB
  //   5
  //   6
  //   011
  //   OR
  //   7
  //   OR
  //   011
  //   8
  //   NOT
  //   100
  //   100
  //   NOT
  //   9
  //   101
  //   SHF
  //   A
  //   SHF
  //   B
  //   101
  //   JPZ
  //   110
  //   C
  //   110
  //   JPO
  //   D
  //   111
  //   GO
  //   E
  //   STR
  //   111
  //   F
  //   Instruction Set
  //   0
  //   AC <= X
  //   1
  //   AC <= M(X)
  //   0
  //   AC <= AC+X
  //   1
  //   AC <= AC+M(X)
  //   0
  //   AC <= AC-X
  //   1
  //   AC <= AC-M(X)
  //   0
  //   AC <= AC OR X
  //   1
  //   AC <= AC OR M(X)
  //   0
  //   AC <= NOT X
  //   1
  //   AC <= NOT M( X)
  //   0
  //   AC <= AC << Q
  //   1
  //   AC <= AC >> Q
  //   0
  //   1
  //   PC <= X
  //   0
  //   1
  //   M(X) <= AC 
  //   PC <= X SE FLAG Z
  //   PC <= X SE FLAG O
  //   contents of rom_1 (hex, n*v repeats v):
  //   0 f0 1 f1 10 31 d0 f2 11 f0 12 f1 e4
endmodule

module Buffer (
  input  [3:0] A,
  input  Control,
  output [3:0] S
);

  assign S[2] = Control ? A[2] : 1'bz;  // Controlled_Buffer controlled_buffer_1
  assign S[3] = Control ? A[3] : 1'bz;  // Controlled_Buffer controlled_buffer_2
  assign S[1] = Control ? A[1] : 1'bz;  // Controlled_Buffer controlled_buffer_3
  assign S[0] = Control ? A[0] : 1'bz;  // Controlled_Buffer controlled_buffer_4
endmodule

module decodificador_3x8 (
  input  [2:0] in_1,
  output S0,
  output S0_2,
  output S2,
  output S3,
  output S4,
  output S5,
  output S6,
  output S7
);

  wire not_1_out, not_2_out, not_3_out, not_4_out, not_5_out, not_6_out, not_7_out, not_8_out, not_9_out,
       not_10_out, not_11_out, not_12_out;

  not not_1 (not_1_out, in_1[2]);
  not not_2 (not_2_out, in_1[1]);
  not not_3 (not_3_out, in_1[0]);
  not not_4 (not_4_out, in_1[2]);
  not not_5 (not_5_out, in_1[1]);
  not not_6 (not_6_out, in_1[2]);
  not not_7 (not_7_out, in_1[0]);
  not not_8 (not_8_out, in_1[2]);
  not not_9 (not_9_out, in_1[1]);
  not not_10 (not_10_out, in_1[0]);
  not not_11 (not_11_out, in_1[1]);
  not not_12 (not_12_out, in_1[0]);
  and and_1 (S0, not_1_out, not_2_out, not_3_out);
  and and_2 (S0_2, not_4_out, not_5_out, in_1[0]);
  and and_3 (S2, not_6_out, in_1[1], not_7_out);
  and and_4 (S3, not_8_out, in_1[1], in_1[0]);
  and and_5 (S4, in_1[2], not_9_out, not_10_out);
  and and_6 (S5, in_1[2], not_11_out, in_1[0]);
  and and_7 (S6, in_1[2], in_1[1], not_12_out);
  and and_8 (S7, in_1[2], in_1[1], in_1[0]);
endmodule

module Add_1 (
  input  A,
  input  B,
  input  C,
  output V,
  output S
);

  wire and_1_out, and_2_out, or_1_out, xor_1_out;

  or or_1 (or_1_out, C, B);
  xor xor_1 (xor_1_out, A, B);
  and and_1 (and_1_out, or_1_out, A);
  and and_2 (and_2_out, B, C);
  xor xor_2 (S, xor_1_out, C);
  or or_2 (V, and_1_out, and_2_out);
endmodule

module Add_4 (
  input  [3:0] A,
  input  [3:0] B,
  output V,
  output [3:0] out_4
);

  wire add_1_2_v, add_1_3_v, add_1_4_v;

  // Probe on A
  Add_1 add_1_1 (.A(add_1_2_v), .B(A[3]), .C(B[3]), .V(V), .S(out_4[3]));
  Add_1 add_1_2 (.A(add_1_3_v), .B(A[2]), .C(B[2]), .V(add_1_2_v), .S(out_4[2]));
  // Probe on out_4
  Add_1 add_1_3 (.A(add_1_4_v), .B(A[1]), .C(B[1]), .V(add_1_3_v), .S(out_4[1]));
  Add_1 add_1_4 (.A(1'b0), .B(A[0]), .C(B[0]), .V(add_1_4_v), .S(out_4[0]));
  // Probe on B
endmodule

module OR (
  input  [3:0] B,
  input  [3:0] A,
  output [3:0] S
);

  or or_1 (S[3], A[3], B[3]);
  or or_2 (S[2], A[2], B[2]);
  or or_3 (S[1], A[1], B[1]);
  or or_4 (S[0], A[0], B[0]);
endmodule

module NOT (
  input  [3:0] B,
  output [3:0] S
);

  not not_1 (S[2], B[2]);
  not not_2 (S[1], B[1]);
  not not_3 (S[3], B[3]);
  not not_4 (S[0], B[0]);
endmodule

module Sub_1 (
  input  A,
  input  B,
  input  VEM_1,
  output S,
  output VAI_1
);

  wire and_1_out, and_2_out, or_1_out, xor_1_out;

  xor xor_1 (xor_1_out, A, B);
  or or_1 (or_1_out, B, VEM_1);
  and and_1 (and_1_out, B, VEM_1);
  xor xor_2 (S, xor_1_out, VEM_1);
  and and_2 (and_2_out, or_1_out, ~A);  // AND_Gate
  or or_2 (VAI_1, and_2_out, and_1_out);
endmodule

module DIR (
  input  [3:0] A,
  input  [1:0] B,
  output [3:0] out_3
);

  wire and_1_out, and_2_out, and_3_out, and_4_out, and_5_out, and_6_out, and_7_out, and_8_out, and_9_out;

  and and_1 (and_1_out, A[3], B[1], B[0]);
  and and_2 (and_2_out, A[2], B[1], ~B[0]);  // AND_Gate
  and and_3 (and_3_out, A[1], ~B[1], B[0]);  // AND_Gate
  and and_4 (and_4_out, A[0], ~B[1], ~B[0]);  // AND_Gate
  and and_5 (and_5_out, A[3], B[1], ~B[0]);  // AND_Gate
  and and_6 (and_6_out, A[2], ~B[1], B[0]);  // AND_Gate
  and and_7 (and_7_out, A[1], ~B[1], ~B[0]);  // AND_Gate
  and and_8 (and_8_out, A[3], ~B[1], B[0]);  // AND_Gate
  and and_9 (and_9_out, A[2], ~B[1], ~B[0]);  // AND_Gate
  and and_10 (out_3[3], A[3], ~B[1], ~B[0]);  // AND_Gate
  or or_1 (out_3[0], and_1_out, and_2_out, and_3_out, and_4_out);
  or or_2 (out_3[1], and_5_out, and_6_out, and_7_out);
  or or_3 (out_3[2], and_8_out, and_9_out);
endmodule

module ESQ (
  input  [3:0] A,
  input  [1:0] B,
  output [3:0] out_3
);

  wire and_1_out, and_2_out, and_3_out, and_4_out, and_5_out, and_6_out, and_7_out, and_8_out, and_9_out;

  and and_1 (and_1_out, A[0], B[1], B[0]);
  and and_2 (and_2_out, A[1], B[1], ~B[0]);  // AND_Gate
  and and_3 (and_3_out, A[2], ~B[1], B[0]);  // AND_Gate
  and and_4 (and_4_out, A[3], ~B[1], ~B[0]);  // AND_Gate
  and and_5 (and_5_out, A[0], B[1], ~B[0]);  // AND_Gate
  and and_6 (and_6_out, A[1], ~B[1], B[0]);  // AND_Gate
  and and_7 (and_7_out, A[2], ~B[1], ~B[0]);  // AND_Gate
  and and_8 (and_8_out, A[0], ~B[1], B[0]);  // AND_Gate
  and and_9 (and_9_out, A[1], ~B[1], ~B[0]);  // AND_Gate
  and and_10 (out_3[0], A[0], ~B[1], ~B[0]);  // AND_Gate
  or or_1 (out_3[3], and_1_out, and_2_out, and_3_out, and_4_out);
  or or_2 (out_3[2], and_5_out, and_6_out, and_7_out);
  or or_3 (out_3[1], and_8_out, and_9_out);
endmodule

module sub_4 (
  input  [3:0] B,
  input  [3:0] A,
  output OVERFLOW,
  output [3:0] \SUBTRAÇÃO 
);

  wire sub_1_1_vai_1, sub_1_3_vai_1, sub_1_4_vai_1;

  // Probe on A
  Sub_1 sub_1_1 (.S(\SUBTRAÇÃO [2]), .VAI_1(sub_1_1_vai_1), .A(A[2]), .B(B[2]), .VEM_1(sub_1_3_vai_1));
  Sub_1 sub_1_2 (.S(\SUBTRAÇÃO [3]), .VAI_1(OVERFLOW), .A(A[3]), .B(B[3]), .VEM_1(sub_1_1_vai_1));
  Sub_1 sub_1_3 (.S(\SUBTRAÇÃO [1]), .VAI_1(sub_1_3_vai_1), .A(A[1]), .B(B[1]), .VEM_1(sub_1_4_vai_1));
  // Probe on \SUBTRAÇÃO 
  Sub_1 sub_1_4 (.S(\SUBTRAÇÃO [0]), .VAI_1(sub_1_4_vai_1), .A(A[0]), .B(B[0]), .VEM_1(1'b0));
  // Probe on B
endmodule

module ULA (
  input  D,
  input  [3:0] A,
  input  [3:0] B,
  input  [2:0] \Operação ,
  output Overflow,
  output [3:0] \Saída ,
  output Zero
);

  wire add_4_1_v, and_1_out, and_2_out, decodificador_3x8_1_s0, decodificador_3x8_1_s0_2,
       decodificador_3x8_1_s2, decodificador_3x8_1_s3, decodificador_3x8_1_s4, decodificador_3x8_1_s5,
       decodificador_3x8_1_s6, decodificador_3x8_1_s7, not_2_out, sub_4_1_overflow;
  wire [3:0] add_4_1_out_4, buffer_7_s, dir_1_out_3, esq_1_out_3, not_1_s, or_2_s, \sub_4_1_subtração ;

  or or_1 (Overflow, and_1_out, and_2_out);
  and and_1 (and_1_out, sub_4_1_overflow, decodificador_3x8_1_s2);
  and and_2 (and_2_out, add_4_1_v, decodificador_3x8_1_s0_2);
  decodificador_3x8 decodificador_3x8_1 (
    .in_1(\Operação ), .S0(decodificador_3x8_1_s0), .S0_2(decodificador_3x8_1_s0_2),
    .S2(decodificador_3x8_1_s2), .S3(decodificador_3x8_1_s3), .S4(decodificador_3x8_1_s4),
    .S5(decodificador_3x8_1_s5), .S6(decodificador_3x8_1_s6), .S7(decodificador_3x8_1_s7));
  Add_4 add_4_1 (.A(A), .B(B), .V(add_4_1_v), .out_4(add_4_1_out_4));
  Buffer buffer_1 (.A(B), .Control(decodificador_3x8_1_s0), .S(\Saída ));
  Buffer buffer_2 (.A(add_4_1_out_4), .Control(decodificador_3x8_1_s0_2), .S(\Saída ));
  sub_4 sub_4_1 (.A(A), .B(B), .\SUBTRAÇÃO (\sub_4_1_subtração ), .OVERFLOW(sub_4_1_overflow));
  Buffer buffer_3 (.A(\sub_4_1_subtração ), .Control(decodificador_3x8_1_s2), .S(\Saída ));
  OR or_2 (.A(A), .B(B), .S(or_2_s));
  Buffer buffer_4 (.A(or_2_s), .Control(decodificador_3x8_1_s3), .S(\Saída ));
  nor nor_1 (Zero, \Saída [0], \Saída [1], \Saída [2], \Saída [3], decodificador_3x8_1_s6, decodificador_3x8_1_s7);
  NOT not_1 (.B(B), .S(not_1_s));
  Buffer buffer_5 (.A(not_1_s), .Control(decodificador_3x8_1_s4), .S(\Saída ));
  Buffer buffer_6 (.A(buffer_7_s), .Control(decodificador_3x8_1_s5), .S(\Saída ));
  DIR dir_1 (.A(A), .out_3(dir_1_out_3), .B(B[1:0]));
  ESQ esq_1 (.A(A), .out_3(esq_1_out_3), .B(B[1:0]));
  Buffer buffer_7 (.A(dir_1_out_3), .Control(not_2_out), .S(buffer_7_s));
  not not_2 (not_2_out, D);
  Buffer buffer_8 (.A(esq_1_out_3), .Control(D), .S(buffer_7_s));
endmodule

module Mux (
  input  [3:0] E0,
  input  [3:0] E1,
  input  Controle,
  output [3:0] S
);

  wire not_1_out;

  not not_1 (not_1_out, Controle);
  Buffer buffer_1 (.A(E0), .Control(not_1_out), .S(S));
  Buffer buffer_2 (.A(E1), .Control(Controle), .S(S));
endmodule

module AC (
  input  [3:0] D,
  input  in_2,
  output [3:0] Q
);

  D_Flip_Flop d_ff_1 (.clk(in_2), .D(D[3]), .Q(Q[3]));  // open: Qn, preset, en, reset
  D_Flip_Flop d_ff_2 (.clk(in_2), .D(D[2]), .Q(Q[2]));  // open: Qn, preset, en, reset
  D_Flip_Flop d_ff_3 (.clk(in_2), .D(D[1]), .Q(Q[1]));  // open: Qn, preset, en, reset
  D_Flip_Flop d_ff_4 (.clk(in_2), .D(D[0]), .Q(Q[0]));  // open: Qn, preset, en, reset
endmodule

module IR (
  input  Clock,
  input  [7:0] D,
  output [7:0] Q
);

  D_Flip_Flop #(.trigger("falling")) d_ff_1 (.clk(Clock), .D(D[7]), .Q(Q[7]));  // open: Qn, preset, en, reset
  D_Flip_Flop #(.trigger("falling")) d_ff_2 (.clk(Clock), .D(D[6]), .Q(Q[6]));  // open: Qn, preset, en, reset
  D_Flip_Flop #(.trigger("falling")) d_ff_3 (.clk(Clock), .D(D[5]), .Q(Q[5]));  // open: Qn, preset, en, reset
  D_Flip_Flop #(.trigger("falling")) d_ff_4 (.clk(Clock), .D(D[4]), .Q(Q[4]));  // open: Qn, preset, en, reset
  D_Flip_Flop #(.trigger("falling")) d_ff_5 (.clk(Clock), .D(D[3]), .Q(Q[3]));  // open: Qn, preset, en, reset
  D_Flip_Flop #(.trigger("falling")) d_ff_6 (.clk(Clock), .D(D[2]), .Q(Q[2]));  // open: Qn, preset, en, reset
  D_Flip_Flop #(.trigger("falling")) d_ff_7 (.clk(Clock), .D(D[1]), .Q(Q[1]));  // open: Qn, preset, en, reset
  D_Flip_Flop #(.trigger("falling")) d_ff_8 (.clk(Clock), .D(D[0]), .Q(Q[0]));  // open: Qn, preset, en, reset
endmodule

module Unidade_de_Controle (
  input  [7:0] \INSTRUÇÃO ,
  input  Clock,
  input  Reset,
  input  ZERO,
  input  Overflow,
  output [3:0] Dados,
  output [3:0] Operando,
  output Clock_IR,
  output Clock_AC,
  output Clock_MEM,
  output D,
  output Reset_PC,
  output Clock_PC,
  output [2:0] OpCode,
  output E,
  output load,
  output LOAD_2
);

  wire and_5_out, GOTO_out, JO_out, JZ_out, not_2_out, STOR_out;
  wire [1:0] counter_1_q;

  Counter #(.width(2), .max('h3)) counter_1 (.Q(counter_1_q), .clk(Clock), .clr(Reset));  // open: load, D, count, carry
  and STOR (STOR_out, \INSTRUÇÃO [7], \INSTRUÇÃO [6], \INSTRUÇÃO [5], \INSTRUÇÃO [4], Clock_AC);
  not not_1 (load, STOR_out);
  and and_1 (Clock_IR, ~counter_1_q[0], ~counter_1_q[1]);  // AND_Gate
  and GOTO (GOTO_out, \INSTRUÇÃO [7], \INSTRUÇÃO [6], \INSTRUÇÃO [5], ~\INSTRUÇÃO [4], Clock_PC);  // AND_Gate
  and and_2 (Clock_PC, counter_1_q[0], ~counter_1_q[1]);  // AND_Gate
  and JO (JO_out, \INSTRUÇÃO [7], \INSTRUÇÃO [6], ~\INSTRUÇÃO [5], \INSTRUÇÃO [4], Clock_PC, Overflow);  // AND_Gate
  and and_3 (Clock_MEM, counter_1_q[0], counter_1_q[1]);
  and and_4 (Clock_AC, ~counter_1_q[0], counter_1_q[1]);  // AND_Gate
  and JZ (JZ_out, \INSTRUÇÃO [7], \INSTRUÇÃO [6], ~\INSTRUÇÃO [5], ~\INSTRUÇÃO [4], Clock_PC, ZERO);  // AND_Gate
  or or_1 (LOAD_2, JZ_out, JO_out, GOTO_out);
  and and_5 (and_5_out, \INSTRUÇÃO [7], ~\INSTRUÇÃO [6], \INSTRUÇÃO [5]);  // AND_Gate
  not not_2 (not_2_out, and_5_out);
  and and_6 (E, not_2_out, \INSTRUÇÃO [4]);

  assign D = \INSTRUÇÃO [4];
  assign Dados = \INSTRUÇÃO [3:0];
  assign OpCode = \INSTRUÇÃO [7:5];
  assign Operando = \INSTRUÇÃO [3:0];
  assign Reset_PC = Reset;
endmodule
