// Logisim project projeto1.circ as structural Verilog: 3 circuits, main circuit main
module main (
  input  [3:0] B,
  input  A,
  input  B_2,
  input  [3:0] A_2,
  input  C,
  output V,
  output V_2,
  output [3:0] S,
  output S_2
);

  Add_1 add_1_1 (.A(C), .B(A), .C(B_2), .V(V), .S(S_2));
  Add_4 add_4_1 ();  // open: A, B, out_4, V
endmodule

// S
module Add_1 (
  input  A,
  input  B,
  input  C,
  output V,
  output S
);

  wire and_1_out, and_2_out, or_1_out, xor_1_out;

  or or_1 (or_1_out, C, B);
  xor xor_1 (xor_1_out, A, B);
  and and_1 (and_1_out, or_1_out, A);
  and and_2 (and_2_out, B, C);
  xor xor_2 (S, xor_1_out, C);
  or or_2 (V, and_1_out, and_2_out);
endmodule

module Add_4 (
  input  [3:0] A,
  input  [3:0] B,
  output V,
  output [3:0] out_4
);

  wire add_1_2_v, add_1_3_v, add_1_4_v;

  // Probe on A
  Add_1 add_1_1 (.A(add_1_2_v), .B(A[3]), .C(B[3]), .V(V), .S(out_4[3]));
  Add_1 add_1_2 (.A(add_1_3_v), .B(A[2]), .C(B[2]), .V(add_1_2_v), .S(out_4[2]));
  // Probe on out_4
  Add_1 add_1_3 (.A(add_1_4_v), .B(A[1]), .C(B[1]), .V(add_1_3_v), .S(out_4[1]));
  Add_1 add_1_4 (.A(1'b0), .B(A[0]), .C(B[0]), .V(add_1_4_v), .S(out_4[0]));
  // Probe on B
endmodule
