// Logisim project projeto_arquiteturacomp3.circ as structural Verilog: 11 circuits, main circuit main
module main (
  input  D,
  input  [3:0] A,
  input  [3:0] B
);

  wire [3:0] add_4_1_out_4, buffer_3_p1, not_1_s, or_1_s;

  Add_4 add_4_1 (.A(A), .B(B), .out_4(add_4_1_out_4));  // open: V
  // Buffer buffer_1: pin names not known; wires that end beside it: B
  // Buffer buffer_2: pin names not known; wires that end beside it: add_4_1_out_4
  Sub_4 sub_4_1 (.A(A), .B(B), .\SUBTRAÇÃO (buffer_3_p1));  // open: OVERFLOW
  // Buffer buffer_3: pin names not known; wires that end beside it: buffer_3_p1
  OR or_1 (.A(A), .B(B), .S(or_1_s));
  // Buffer buffer_4: pin names not known; wires that end beside it: or_1_s
  NOT not_1 (.B(B), .S(not_1_s));
  // Buffer buffer_5: pin names not known; wires that end beside it: not_1_s
  // DIR dir_1: pin names not known; wires that end beside it: A, B[1:0]
  // ESQ esq_1: pin names not known; wires that end beside it: A, B[1:0]
endmodule

module Buffer (
  input  [3:0] A,
  input  Control,
  output [3:0] S
);

  buf buffer_1 (S[2], A[2]);
  buf buffer_2 (S[3], A[3]);
  buf buffer_3 (S[1], A[1]);
  buf buffer_4 (S[0], A[0]);
endmodule

module decodificador_3x8 (
  input  [2:0] in_1,
  output S0,
  output S0_2,
  output S2,
  output S3,
  output S4,
  output S5,
  output S6,
  output S7
);

  wire not_1_out, not_2_out, not_3_out, not_4_out, not_5_out, not_6_out, not_7_out, not_8_out, not_9_out,
       not_10_out, not_11_out, not_12_out;

  not not_1 (not_1_out, in_1[2]);
  not not_2 (not_2_out, in_1[1]);
  not not_3 (not_3_out, in_1[0]);
  not not_4 (not_4_out, in_1[2]);
  not not_5 (not_5_out, in_1[1]);
  not not_6 (not_6_out, in_1[2]);
  not not_7 (not_7_out, in_1[0]);
  not not_8 (not_8_out, in_1[2]);
  not not_9 (not_9_out, in_1[1]);
  not not_10 (not_10_out, in_1[0]);
  not not_11 (not_11_out, in_1[1]);
  not not_12 (not_12_out, in_1[0]);
  and and_1 (S0, not_1_out, not_2_out, not_3_out);
  and and_2 (S0_2, not_4_out, not_5_out, in_1[0]);
  and and_3 (S2, not_6_out, in_1[1], not_7_out);
  and and_4 (S3, not_8_out, in_1[1], in_1[0]);
  and and_5 (S4, in_1[2], not_9_out, not_10_out);
  and and_6 (S5, in_1[2], not_11_out, in_1[0]);
  and and_7 (S6, in_1[2], in_1[1], not_12_out);
  and and_8 (S7, in_1[2], in_1[1], in_1[0]);
endmodule

module Add_1 (
  input  A,
  input  B,
  input  C,
  output V,
  output S
);

  wire and_1_out, and_2_out, or_1_out, xor_1_out;

  or or_1 (or_1_out, C, B);
  xor xor_1 (xor_1_out, A, B);
  and and_1 (and_1_out, or_1_out, A);
  and and_2 (and_2_out, B, C);
  xor xor_2 (S, xor_1_out, C);
  or or_2 (V, and_1_out, and_2_out);
endmodule

module Add_4 (
  input  [3:0] A,
  input  [3:0] B,
  output V,
  output [3:0] out_4
);

  wire add_1_2_v, add_1_3_v, add_1_4_v;

  // Probe on A
  Add_1 add_1_1 (.A(add_1_2_v), .B(A[3]), .C(B[3]), .V(V), .S(out_4[3]));
  Add_1 add_1_2 (.A(add_1_3_v), .B(A[2]), .C(B[2]), .V(add_1_2_v), .S(out_4[2]));
  // Probe on out_4
  Add_1 add_1_3 (.A(add_1_4_v), .B(A[1]), .C(B[1]), .V(add_1_3_v), .S(out_4[1]));
  Add_1 add_1_4 (.A(1'b0), .B(A[0]), .C(B[0]), .V(add_1_4_v), .S(out_4[0]));
  // Probe on B
endmodule

module OR (
  input  [3:0] B,
  input  [3:0] A,
  output [3:0] S
);

  or or_1 (S[2], A[2], B[2]);
  or or_2 (S[3], A[3], B[3]);
  or or_3 (S[1], A[1], B[1]);
  or or_4 (S[0], A[0], B[0]);
endmodule

module NOT (
  input  [3:0] B,
  output [3:0] S
);

  not not_1 (S[2], B[2]);
  not not_2 (S[1], B[1]);
  not not_3 (S[3], B[3]);
  not not_4 (S[0], B[0]);
endmodule

module Sub_4 (
  input  [3:0] B,
  input  [3:0] A,
  input  [3:0] \SUBTRAÇÃO ,
  output OVERFLOW
);

  wire sub_1_1_vai_1, sub_1_3_vai_1, sub_1_4_vai_1;

  // Probe on A
  Sub_1 sub_1_1 (.S(\SUBTRAÇÃO [2]), .VAI_1(sub_1_1_vai_1), .A(A[2]), .B(B[2]), .VEM_1(sub_1_3_vai_1));
  Sub_1 sub_1_2 (.S(\SUBTRAÇÃO [3]), .VAI_1(OVERFLOW), .A(A[3]), .B(B[3]), .VEM_1(sub_1_1_vai_1));
  Sub_1 sub_1_3 (.S(\SUBTRAÇÃO [1]), .VAI_1(sub_1_3_vai_1), .A(A[1]), .B(B[1]), .VEM_1(sub_1_4_vai_1));
  // Probe on \SUBTRAÇÃO 
  Sub_1 sub_1_4 (.S(\SUBTRAÇÃO [0]), .VAI_1(sub_1_4_vai_1), .A(A[0]), .B(B[0]), .VEM_1(1'b0));
  // Probe on B
endmodule

module Sub_1 (
  input  A,
  input  B,
  input  VEM_1,
  output S,
  output VAI_1
);

  wire and_1_out, and_2_out, or_1_out, xor_1_out;

  xor xor_1 (xor_1_out, A, B);
  or or_1 (or_1_out, B, VEM_1);
  and and_1 (and_1_out, B, VEM_1);
  xor xor_2 (S, xor_1_out, VEM_1);
  and and_2 (and_2_out, or_1_out, ~A);  // AND_Gate
  or or_2 (VAI_1, and_2_out, and_1_out);
endmodule

module DIR (
  input  [3:0] A,
  input  [1:0] B,
  output [3:0] out_3
);

  wire and_1_out, and_2_out, and_3_out, and_4_out, and_5_out, and_6_out, and_7_out, and_8_out, and_9_out;

  and and_1 (and_1_out, A[3], B[1], B[0]);
  and and_2 (and_2_out, A[2], B[1], ~B[0]);  // AND_Gate
  and and_3 (and_3_out, A[1], ~B[1], B[0]);  // AND_Gate
  and and_4 (and_4_out, A[0], ~B[1], ~B[0]);  // AND_Gate
  and and_5 (and_5_out, A[3], B[1], ~B[0]);  // AND_Gate
  and and_6 (and_6_out, A[2], ~B[1], B[0]);  // AND_Gate
  and and_7 (and_7_out, A[1], ~B[1], ~B[0]);  // AND_Gate
  and and_8 (and_8_out, A[3], ~B[1], B[0]);  // AND_Gate
  and and_9 (and_9_out, A[2], ~B[1], ~B[0]);  // AND_Gate
  and and_10 (out_3[3], A[3], ~B[1], ~B[0]);  // AND_Gate
  or or_1 (out_3[0], and_1_out, and_2_out, and_3_out, and_4_out);
  or or_2 (out_3[1], and_5_out, and_6_out, and_7_out);
  or or_3 (out_3[2], and_8_out, and_9_out);
endmodule

module ESQ (
  input  [3:0] A,
  input  [1:0] B,
  output [3:0] out_3
);

  wire and_1_out, and_2_out, and_3_out, and_4_out, and_5_out, and_6_out, and_7_out, and_8_out, and_9_out;

  and and_1 (and_1_out, A[0], B[1], B[0]);
  and and_2 (and_2_out, A[1], B[1], ~B[0]);  // AND_Gate
  and and_3 (and_3_out, A[2], ~B[1], B[0]);  // AND_Gate
  and and_4 (and_4_out, A[3], ~B[1], ~B[0]);  // AND_Gate
  and and_5 (and_5_out, A[0], B[1], ~B[0]);  // AND_Gate
  and and_6 (and_6_out, A[1], ~B[1], B[0]);  // AND_Gate
  and and_7 (and_7_out, A[2], ~B[1], ~B[0]);  // AND_Gate
  and and_8 (and_8_out, A[0], ~B[1], B[0]);  // AND_Gate
  and and_9 (and_9_out, A[1], ~B[1], ~B[0]);  // AND_Gate
  and and_10 (out_3[0], A[0], ~B[1], ~B[0]);  // AND_Gate
  or or_1 (out_3[3], and_1_out, and_2_out, and_3_out, and_4_out);
  or or_2 (out_3[2], and_5_out, and_6_out, and_7_out);
  or or_3 (out_3[1], and_8_out, and_9_out);
endmodule
